# Fritzing sketch Project (saved by Fritzing 0.9.3b)
breadboards: 1

parts:
  Part1 = Arduino Uno (Rev3)
  Mat3 = LED Matrix - Serial Interface - Red/Green/Blue
  Mat2 = LED Matrix - Serial Interface - Red/Green/Blue
  Mat1 = LED Matrix - Serial Interface - Red/Green/Blue
  R1 = Resistor [tolerance=±5% resistance=100k package="0603 [SMD]"]
  B1 = Momentary Switch [package=ksa_sealed_tac_switch]
  B2 = Momentary Switch [package=ksa_sealed_tac_switch]
  B3 = Momentary Switch [package=ksa_sealed_tac_switch]
  B4 = Momentary Switch [package=ksa_sealed_tac_switch]
  R2 = Resistor [tolerance=±5% resistance=100k package="0603 [SMD]"]
  R3 = Resistor [tolerance=±5% resistance=100k package="0603 [SMD]"]
  R4 = Resistor [tolerance=±5% resistance=100k package="0603 [SMD]"]
  Mat4 = LED Matrix - Serial Interface - Red/Green/Blue

nets:
  N1: Part1.D9_PWM, Mat3.SCK, Mat2.SCK, Mat1.SCK, Mat4.SCK
  N2: Part1.D10_PWM/SS, Mat3.CS, Mat2.CS, Mat1.CS, Mat4.CS
  N3: Part1.D11_PWM/MOSI, Mat1.MOSI
  GND: Part1.GND, Mat3.GND, Mat2.GND, Mat1.GND, R1.Pin_1, R2.Pin_1, R3.Pin_1, R4.Pin_1, Mat4.GND
  N4: Part1.D2, B4.1
  N5: Part1.D3_PWM, B3.1
  N6: Part1.D4, B2.1
  N7: Part1.D5_PWM, B1.1
  VCC: Part1.5V, Mat3.VCC, Mat2.VCC, Mat1.VCC, Mat4.VCC
  N8: Mat3.MISO, Mat4.MOSI
  N9: Mat3.MOSI, Mat2.MISO
  N10: Mat2.MOSI, Mat1.MISO
  N11: R1.Pin_0, B1.3
  N12: B2.3, R2.Pin_0
  N13: B3.3, R3.Pin_0
  N14: B4.3, R4.Pin_0
